// Logisim project cpu.circ as structural Verilog: 4 circuits, main circuit main
module main (
);

  wire button_1_out, button_2_out, clock, counter_1_q, counter_2_q, FDX_state_0, FDX_state_1, not_1_out,
       not_2_out, not_3_out, not_4_out, select_RAM_address, write_AC, write_PC, write_RAM;
  wire [7:0] AC_q, bitselector_1_out, multiplexer_1_out, PC, UC_output;
  wire [15:0] IR_q, RAM, to_RAM;

  Clock clock_1 (.out(clock));
  Counter #(.width(1), .max('h1)) counter_1 (.Q(counter_1_q), .clk(clock));  // open: load, D, count, carry, clr
  Counter #(.width(1), .max('h1)) counter_2 (.Q(counter_2_q), .clk(not_1_out));  // open: load, D, count, carry, clr
  not not_1 (not_1_out, clock);
  not not_2 (not_2_out, counter_1_q);
  not not_3 (not_3_out, counter_2_q);
  BitSelector #(.width(16), .group(8)) bitselector_1 (.in(RAM), .out(bitselector_1_out), .sel(1'b0));
  UC uc_1 (
    .IR(IR_q), .clock(FDX_state_1), .select_RAM_address(select_RAM_address), .write_AC(write_AC),
    .out_6(UC_output), .write_RAM(write_RAM));
  Register #(.width(16)) IR (.D(RAM), .Q(IR_q), .clk(FDX_state_0));  // open: en, clr
  and and_1 (FDX_state_0, not_2_out, clock);
  and and_2 (FDX_state_1, counter_1_q, not_3_out);
  Register AC (.D(bitselector_1_out), .en(write_AC), .Q(AC_q), .clk(FDX_state_1), .clr(button_1_out));
  assign to_RAM = {{8{1'b0}}, AC_q};  // Bit_Extender bit_extender_1
  Button button_1 (.out(button_1_out));
  Multiplexer #(.width(8)) multiplexer_1 (
    .in0(PC), .in1(UC_output), .out(multiplexer_1_out), .sel(select_RAM_address));  // open: en
  not not_4 (not_4_out, write_PC);
  // ula ula_1: pin names not known
  Counter u_PC (.load(write_PC), .count(not_4_out), .Q(PC), .clk(FDX_state_1), .clr(button_2_out));  // open: D, carry
  RAM #(.dataWidth(16), .bus("separate")) ram_1 (
    .addr(multiplexer_1_out), .din(to_RAM), .data(RAM), .str(write_RAM), .clk(FDX_state_1));  // open: sel, ld, clr
  Button button_2 (.out(button_2_out));

  // Notes on the sheet:
  //   <------------
  //   conectando o clock diretamente
  //   chegávamos a problemas de delay
endmodule

module UC (
  input  [15:0] IR,
  input  clock,
  output select_RAM_address,
  output write_AC,
  output write_RAM,
  output [7:0] out_6
);

  wire decoder_1_out0, decoder_1_out1, decoder_1_out2, decoder_1_out3, decoder_1_out5, decoder_1_out6,
       decoder_1_out7, decoder_1_out8, decoder_1_out9, decoder_1_out10, decoder_1_out11, decoder_1_out12,
       decoder_1_out14, decoder_1_out15, select_RAM_address_1, select_RAM_address_2;

  Decoder #(.select(4)) decoder_1 (
    .out0(decoder_1_out0), .out1(decoder_1_out1), .out2(decoder_1_out2), .out3(decoder_1_out3),
    .out5(decoder_1_out5), .out6(decoder_1_out6), .out7(decoder_1_out7), .out8(decoder_1_out8),
    .out9(decoder_1_out9), .out10(decoder_1_out10), .out11(decoder_1_out11), .out12(decoder_1_out12),
    .out13(decoder_1_out12), .out14(decoder_1_out14), .out15(decoder_1_out15), .sel(IR[11:8]), .en(1'b1));  // open: out4
  op1 op1_1 (.enable(decoder_1_out1), .select_RAM_address(select_RAM_address_1), .write_AC(write_AC));
  op2 op2_1 (.enable(decoder_1_out2), .select_RAM_address(select_RAM_address_2), .write_RAM(write_RAM));
  or or_1 (select_RAM_address, select_RAM_address_1, select_RAM_address_2);

  assign out_6 = IR[7:0];

  // Other names for the same wires on the sheet: instruction[3:0] = IR[11:8]; complement[7:0] = IR[7:0]
endmodule

module op1 (
  input  enable,
  output select_RAM_address,
  output write_AC
);


  assign select_RAM_address = enable;
  assign write_AC = enable;
endmodule

module op2 (
  input  enable,
  output select_RAM_address,
  output write_RAM
);


  assign select_RAM_address = enable;
  assign write_RAM = enable;
endmodule
